# Fritzing sketch controlbox (saved by Fritzing 0.9.3b)
breadboards: 1

parts:
  Part1 = Arduino Mega 2560 (Rev3)
  8_Channel_Relay1 = 8 Channel Power Relay
  Load_Cell1 = Load Cell - Red/white/black/green
  Part2 = HX711 Weighing Sensor Module
  AM1 = AM2302 Humidity and Temperature Sensor
  Load_Cell2 = Load Cell - Red/white/black/green
  Part3 = HX711 Weighing Sensor Module
  Load_Cell3 = Load Cell - Red/white/black/green
  Part4 = HX711 Weighing Sensor Module
  Load_Cell4 = Load Cell - Red/white/black/green
  Part5 = HX711 Weighing Sensor Module
  Load_Cell5 = Load Cell - Red/white/black/green
  Part6 = HX711 Weighing Sensor Module
  PS1 = Meanwell Power Supply LRS-100-5 [part_number=LRS-100-5]
  PS2 = Meanwell Power Supply LRS-100-5 [part_number=LRS-100-5]
  Mod1 = Raspberry Pi 4B  # not connected

nets:
  N1: Part1.A8, Part4.DO/RX
  N2: Part1.A9, Part4.CK/TX
  N3: Part1.A10, Part5.DO/RX
  N4: Part1.A11, Part5.CK/TX
  N5: Part1.A12, Part6.DO/RX
  N6: Part1.A13, Part6.CK/TX
  N7: Part1.A3, AM1.DATA
  N8: Part1.A4, Part2.DO/RX
  N9: Part1.A5, Part2.CK/TX
  N10: Part1.A6, Part3.DO/RX
  N11: Part1.A7, Part3.CK/TX
  VCC: Part1.5V, 8_Channel_Relay1.VCC, Part2.VCC, AM1.VDD, Part3.VCC, Part4.VCC, Part5.VCC, Part6.VCC
  GND: Part1.GND, Part2.GND, AM1.GND, Part3.GND, Part4.GND, Part5.GND, Part6.GND, PS1.connector4
  N12: Part1.VIN, PS1.connector6
  N13: Part1.D22, 8_Channel_Relay1.IN1
  N14: Part1.D24, 8_Channel_Relay1.IN2
  N15: Part1.D26, 8_Channel_Relay1.IN3
  N16: Part1.D28, 8_Channel_Relay1.IN4
  N17: Part1.D30, 8_Channel_Relay1.IN5
  N18: Part1.D32, 8_Channel_Relay1.IN6
  N19: Part1.D34, 8_Channel_Relay1.IN7
  N20: Part1.D36, 8_Channel_Relay1.IN8
  N21: 8_Channel_Relay1.GND, PS2.connector4
  N22: 8_Channel_Relay1.JD-VCC, PS2.connector6
  N23: Load_Cell1.wire1, Part2.E+
  N24: Load_Cell1.wire2, Part2.A+
  N25: Load_Cell1.wire3, Part2.E-
  N26: Load_Cell1.wire4, Part2.A-
  N27: Load_Cell2.wire1, Part3.E+
  N28: Load_Cell2.wire2, Part3.A+
  N29: Load_Cell2.wire3, Part3.E-
  N30: Load_Cell2.wire4, Part3.A-
  N31: Load_Cell3.wire1, Part4.E+
  N32: Load_Cell3.wire2, Part4.A+
  N33: Load_Cell3.wire3, Part4.E-
  N34: Load_Cell3.wire4, Part4.A-
  N35: Load_Cell4.wire1, Part5.E+
  N36: Load_Cell4.wire2, Part5.A+
  N37: Load_Cell4.wire3, Part5.E-
  N38: Load_Cell4.wire4, Part5.A-
  N39: Load_Cell5.wire1, Part6.E+
  N40: Load_Cell5.wire2, Part6.A+
  N41: Load_Cell5.wire3, Part6.E-
  N42: Load_Cell5.wire4, Part6.A-

notes:
  RELAYS
  LOAD CELLS
  DHT SENSOR
  POWER SUPPLY ARDUINO
  POWER SUPPLY RELAYS
  RASPBERRY PI4

custom parts:
  8 Channel Power Relay: An 8 channel power relay. The module operates at 5V.
  Load Cell - Red/white/black/green: A rectangle load cell/weighting pressure Sensor with four wires - Red, white, black, green. Normally corresponding with E+, E-, A+, A- respectively.

// code stored in the sketch: controllbox.ino
#include "ArduinoJson.h"

///////////////////////////////////////////////
////    LOADCELL MOVING AVERAGES
///////////////////////////////////////////////
// Weight is not expected to change suddenly so moving average smooths any errors and help with drift.
#include <movingAvg.h> 
movingAvg avgloadcell_1(30);
movingAvg avgloadcell_2(30);
movingAvg avgloadcell_3(30);
movingAvg avgloadcell_4(30);
movingAvg avgloadcell_5(30);

///////////////////////////////////////////////
////    RELAYS / RELAY PIN NUMBERS
///////////////////////////////////////////////
  const int light_relayenable = 22;
  const int cool_relayenable = 23;
  const int heat_relayenable = 24;

  const int humidify_relayenable = 25;
  const int dehumidify_relayenable = 26;
  const int airpump_relayenable = 27;
  const int circulate_relayenable = 28;
  
///////////////////////////////////////////////
////    TIMER
///////////////////////////////////////////////
#include <arduino-timer.h>;
auto timer = timer_create_default();
Timer<> default_timer; // save as above

///////////////////////////////////////////////
////    DHT SENSOR
///////////////////////////////////////////////
// REQUIRES the following Arduino libraries:
// - DHT Sensor Library: https://github.com/adafruit/DHT-sensor-library
// - Adafruit Unified Sensor Lib: https://github.com/adafruit/Adafruit_Sensor
#include "DHT.h"
#define DHTPIN 2
// Uncomment whatever type you're using!
//#define DHTTYPE DHT11   // DHT 11
//#define DHTTYPE DHT22   // DHT 22  (AM2302), AM2321
#define DHTTYPE DHT21   // DHT 21 (AM2301)
// Initialize DHT sensor.
DHT dht(DHTPIN, DHTTYPE);

///////////////////////////////////////////////
////    LOAD CELL
///////////////////////////////////////////////
#include <HX711_ADC.h>

unsigned long stabilizingtime = 5000; // tare preciscion can be improved by adding a few seconds of stabilizing time

//pins:
const int HX711_dout_1 = 4; //HX711 dout pin
const int HX711_sck_1 = 5; //HX711 sck pin

const int HX711_dout_2 = 6; //HX711 dout pin
const int HX711_sck_2 = 7; //HX711 sck pin

const int HX711_dout_3 = 8; //HX711 dout pin
const int HX711_sck_3 = 9; //HX711 sck pin

const int HX711_dout_4 = 10; //HX711 dout pin
const int HX711_sck_4 = 11; //HX711 sck pin

const int HX711_dout_5 = 12; //HX711 dout pin
const int HX711_sck_5 = 13; //HX711 sck pin

//HX711 constructor (dout pin, sck pin)
HX711_ADC LoadCell_1(HX711_dout_1, HX711_sck_1); //HX711 1
HX711_ADC LoadCell_2(HX711_dout_2, HX711_sck_2); //HX711 2
HX711_ADC LoadCell_3(HX711_dout_3, HX711_sck_3); //HX711 3
HX711_ADC LoadCell_4(HX711_dout_4, HX711_sck_4); //HX711 4
HX711_ADC LoadCell_5(HX711_dout_5, HX711_sck_5); //HX711 5

unsigned long t = 0;

///////////////////////////////////////////////
////    COMMAND HANDLER
///////////////////////////////////////////////
#include "CommandHandler.h"
CommandHandler<15> SerialCommandHandler;

///////////////////////////////////////////////
////    DEBUG - Comment out to stop verbose serial output
///////////////////////////////////////////////
#define DEBUG


/* Arrange your settings in this struct. Ensure that 'checksum' is the */
/* last item and is an unsigned int. Otherwise, do whatever you like. */
/* https://gitlab.com/snippets/1728275 */

struct meat_settings {
  float temperature_target;
  float temperature_variance;
  
  float humidity_target;
  float humidity_variance;

  float load_calibration_1;
  float load_calibration_2;
  float load_calibration_3;
  float load_calibration_4;
  float load_calibration_5;

  long tare_offset_1;
  long tare_offset_2;
  long tare_offset_3;
  long tare_offset_4;
  long tare_offset_5;
  
  float cycle_delay = 10*1000*60; //10 minutes

  void Reset() {
  temperature_target = 5;
  temperature_variance = 2;
  
  humidity_target = 80;
  humidity_variance = 4;

  load_calibration_1 = 250.055;
  load_calibration_2 = 250.055;
  load_calibration_3 = 250.055;
  load_calibration_4 = 250.055;
  load_calibration_5 = 250.055;

  tare_offset_1 = 8409015;
  tare_offset_2 = 8409015;
  tare_offset_3 = 8409015;
  tare_offset_4 = 8409015;
  tare_offset_5 = 8409015;
  
  cycle_delay = 10*1000*60; //10 minutes
  
}
  //unsigned int checksum;
};

///////////////////////////////////////////////
////    EEPROM
///////////////////////////////////////////////
#include "EEPROMStore.h"
EEPROMStore<meat_settings> settings;

///////////////////////////////////////////////
////    STATE STRUCT
///////////////////////////////////////////////
struct meat_state {
  float temperature;
  float humidity;
  
  boolean light;
  boolean cool;
  boolean heat;

  boolean humidify;
  boolean dehumidify;
  boolean airpump;
  boolean circulate;
  boolean isactive;
  float loadcells[5];

  boolean tareloadcell_1;
  boolean tareloadcell_2;
  boolean tareloadcell_3;
  boolean tareloadcell_4;
  boolean tareloadcell_5;

  boolean newdataloadcell_1;
  boolean newdataloadcell_2;
  boolean newdataloadcell_3;
  boolean newdataloadcell_4;
  boolean newdataloadcell_5;
};
/* 'state' has to be globally available, so declare it here */
meat_state state;


//Default State
void defaultState(){
  state.temperature = 0;
  state.humidity = 0;
  
  state.light = false;
  state.cool = false;
  state.heat = false;
  state.humidify = false;
  state.dehumidify = false;
  state.airpump = false;
  state.circulate = false;
  state.isactive = true;
  state.loadcells[0]  = 0;
  state.loadcells[1]  = 0;
  state.loadcells[2]  = 0;
  state.loadcells[3]  = 0;
  state.loadcells[4]  = 0;

  state.tareloadcell_1 = false;
  state.tareloadcell_2 = false;
  state.tareloadcell_3 = false;
  state.tareloadcell_4 = false;
  state.tareloadcell_5 = false;

  state.newdataloadcell_1 = false;
  state.newdataloadcell_2 = false;
  state.newdataloadcell_3 = false;
  state.newdataloadcell_4 = false;
  state.newdataloadcell_5 = false;
}

//Command handling
void Cmd_ListAll(CommandParameter &Parameters)
{
  Serial.print(F("OnTime [ms]="));
  //Serial.println(OnTime);
}

void Cmd_Unknown()
{
  // Allocate the JSON document
  StaticJsonDocument<200> JsonResponse;
  JsonResponse["success"] = false;
  JsonResponse["message"] = "I don't understand";
  serializeJson(JsonResponse, Serial);
}

void Cmd_Echo(CommandParameter &Parameters)
{
  // Allocate the JSON document
  StaticJsonDocument<200> JsonResponse;
  JsonResponse["success"] = true;
  JsonResponse["message"] = Parameters.NextParameter();
  serializeJson(JsonResponse, Serial);
  Serial.println();
}
void Cmd_SetTemperatureTarget(CommandParameter &Parameters)
{
  // Allocate the JSON document
  StaticJsonDocument<200> JsonResponse;
  
  float newtemptarget = atof(Parameters.NextParameter());
  #ifdef DEBUG
    Serial.println(newtemptarget);
  #endif
  if (newtemptarget != 0.00){
    settings.Data.temperature_target = newtemptarget;
    
    JsonResponse["success"] = true;
    JsonResponse["message"] = "Target Temperature";
    JsonResponse["target_temp"] = settings.Data.temperature_target;
    serializeJson(JsonResponse, Serial);
    Serial.println();
    settings.Save();
  }else{
    JsonResponse["success"] = false;
    JsonResponse["message"] = "Could Not Set New Temperature Target";
    serializeJson(JsonResponse, Serial);
    Serial.println();
  }
}

void Cmd_SetTemperatureVariance(CommandParameter &Parameters)
{
  // Allocate the JSON document
  StaticJsonDocument<200> JsonResponse;
  
  float newtempvariance = atof(Parameters.NextParameter());
  #ifdef DEBUG
    Serial.println(newtempvariance);
  #endif
  if (newtempvariance != 0.00){
    settings.Data.temperature_variance = newtempvariance;
    
    JsonResponse["success"] = true;
    JsonResponse["message"] = "Temperature Variance";
    JsonResponse["target_temp"] = settings.Data.temperature_variance;
    serializeJson(JsonResponse, Serial);
    Serial.println();
    settings.Save();
  }else{
    JsonResponse["success"] = false;
    JsonResponse["message"] = "Could Not Set New Temperature Variance";
    serializeJson(JsonResponse, Serial);
    Serial.println();
  }
}

void Cmd_SetHumidityTarget(CommandParameter &Parameters)
{
  // Allocate the JSON document
  StaticJsonDocument<200> JsonResponse;
  
  float newhumidity = atof(Parameters.NextParameter());
  #ifdef DEBUG
    Serial.println(newhumidity);
  #endif
  if (newhumidity != 0.00){
    settings.Data.humidity_target = newhumidity;
    
    JsonResponse["success"] = true;
    JsonResponse["message"] = "Target Humidity";
    JsonResponse["target_humidity"] = settings.Data.humidity_target;
    serializeJson(JsonResponse, Serial);
    Serial.println();
    settings.Save();
  }else{
    JsonResponse["success"] = false;
    JsonResponse["message"] = "Could Not Set New Humidity Target";
    serializeJson(JsonResponse, Serial);
    Serial.println();
  }
}

void Cmd_SetHumidityVariance(CommandParameter &Parameters)
{
  // Allocate the JSON document
  StaticJsonDocument<200> JsonResponse;
  
  float newhumidityvariance = atof(Parameters.NextParameter());
  #ifdef DEBUG
    Serial.println(newhumidityvariance);
  #endif
  if (newhumidityvariance != 0.00){
    settings.Data.humidity_variance = newhumidityvariance;
    
    JsonResponse["success"] = true;
    JsonResponse["message"] = "Humidity Variance";
    JsonResponse["target_temp"] = settings.Data.humidity_variance;
    serializeJson(JsonResponse, Serial);
    Serial.println();
    settings.Save();
  }else{
    JsonResponse["success"] = false;
    JsonResponse["message"] = "Could Not Set New Humidity Variance";
    serializeJson(JsonResponse, Serial);
    Serial.println();
  }
}

void Cmd_Set(CommandParameter &Parameters)
{
  // Allocate the JSON document
  StaticJsonDocument<200> JsonResponse;
  
  //Serial.println(Parameters.NextParameter());
  const char* service = Parameters.NextParameter();
  int setstate = atoi(Parameters.NextParameter());
  
  #ifdef DEBUG
  Serial.print("CHECK->");
  Serial.println(service);
  #endif
  
  JsonResponse["success"] = true;
  if(strcmp(service, "light") == 0)
  {
      JsonResponse["message"] = "Light";
      if (setstate == 1){
        state.light = true;
        digitalWrite( light_relayenable , LOW);
      }else if(setstate == 0){
        state.light = false;
        digitalWrite( light_relayenable , HIGH);
      }
      JsonResponse["light"] = state.light;
  }
  else if(strcmp(service, "cool") == 0)
  {
      JsonResponse["message"] = "Cool";
      if (setstate == 1){
        state.cool = true;
        digitalWrite( cool_relayenable , LOW);
      }else if(setstate == 0){
        state.cool = false;
        digitalWrite( cool_relayenable , HIGH);
      }
      JsonResponse["cool"] = state.cool;
  }
  else if(strcmp(service, "heat") == 0)
  {
      JsonResponse["message"] = "Heat";
      if (setstate == 1){
        state.light = true;
        digitalWrite( light_relayenable , LOW);
      }else if(setstate == 0){
        state.light = false;
        digitalWrite( light_relayenable , HIGH);
      }
      JsonResponse["heat"] = state.heat;
  }
  else if(strcmp(service, "humidify") == 0)
  {
      JsonResponse["message"] = "Humidify";
      if (setstate == 1){
        state.humidify = true;
        digitalWrite( humidify_relayenable , LOW);
      }else if(setstate == 0){
        state.humidify = false;
        digitalWrite( humidify_relayenable , HIGH);
      }
      JsonResponse["humidify"] = state.humidify;
  }
  else if(strcmp(service, "dehumidify") == 0)
  {
      JsonResponse["message"] = "Dehumidify";
      if (setstate == 1){
        state.dehumidify = true;
        digitalWrite( dehumidify_relayenable , LOW);
      }else if(setstate == 0){
        state.dehumidify = false;
        digitalWrite( dehumidify_relayenable , HIGH);
      }
      JsonResponse["dehumidify"] = state.dehumidify;
  }
  else if(strcmp(service, "airpump") == 0)
  {
      JsonResponse["message"] = "Airpump";
      if (setstate == 1){
        state.airpump = true;
        digitalWrite( airpump_relayenable , LOW);
      }else if(setstate == 0){
        state.airpump = false;
        digitalWrite( airpump_relayenable , HIGH);
      }
      JsonResponse["airpump"] = state.airpump;
  }
  else if(strcmp(service, "circulate") == 0)
  {
      JsonResponse["message"] = "Circulate";
      if (setstate == 1){
        state.circulate = true;
        digitalWrite( circulate_relayenable , LOW);
      }else if(setstate == 0){
        state.circulate = false;
        digitalWrite( circulate_relayenable , HIGH);
      }
      JsonResponse["circulate"] = state.circulate;
  }
  else if(strcmp(service, "isactive") == 0)
  {
      JsonResponse["message"] = "Isactive";
      if (setstate == 1){
        state.isactive = true;
      }else if(setstate == 0){
        state.isactive = false;
      }
      JsonResponse["isactive"] = state.isactive;
  }
  else
  {
      JsonResponse["success"] = false;
      JsonResponse["message"] = strcat ("No valid service specified: ", service);
  }
  
  serializeJson(JsonResponse, Serial);
  Serial.println();
}

void Cmd_Get(CommandParameter &Parameters)
{
  // Allocate the JSON document
  StaticJsonDocument<200> JsonResponse;
  
  //Serial.println(Parameters.NextParameter());
  const char* service = Parameters.NextParameter();
  Serial.print("CHECK->");
  Serial.println(service);

  JsonResponse["success"] = true;
  if (strcmp(service, "temperature") == 0)
  {
      JsonResponse["message"] = "Temperature";
      JsonResponse["temperature"] = state.temperature;
  }
  else if(strcmp(service, "humidity") == 0)
  {
      JsonResponse["message"] = "Humidity";
      JsonResponse["humidity"] = state.humidity;
  }
  else if(strcmp(service, "light") == 0)
  {
      JsonResponse["message"] = "Light";
      JsonResponse["light"] = state.light;
  }
  else if(strcmp(service, "cool") == 0)
  {
      JsonResponse["message"] = "Cool";
      JsonResponse["cool"] = state.cool;
  }
  else if(strcmp(service, "heat") == 0)
  {
      JsonResponse["message"] = "Heat";
      JsonResponse["heat"] = state.heat;
  }
  else if(strcmp(service, "humidify") == 0)
  {
      JsonResponse["message"] = "Humidify";
      JsonResponse["humidify"] = state.humidify;
  }
  else if(strcmp(service, "dehumidify") == 0)
  {
      JsonResponse["message"] = "Dehumidify";
      JsonResponse["dehumidify"] = state.dehumidify;
  }
  else if(strcmp(service, "airpump") == 0)
  {
      JsonResponse["message"] = "Airpump";
      JsonResponse["airpump"] = state.airpump;
  }
  else if(strcmp(service, "circulate") == 0)
  {
      JsonResponse["message"] = "Circulate";
      JsonResponse["circulate"] = state.circulate;
  }
  else if(strcmp(service, "isactive") == 0)
  {
      JsonResponse["message"] = "Isactive";
      JsonResponse["isactive"] = state.isactive;
  }
  else if(strcmp(service, "loadcells") == 0)
  {
      JsonResponse["message"] = "Loadcells";
      JsonArray data = JsonResponse.createNestedArray("loadcells");
      data.add(state.loadcells[0]);
      data.add(state.loadcells[1]);
      data.add(state.loadcells[2]);
      data.add(state.loadcells[3]);
      data.add(state.loadcells[4]);
  }
  else
  {
      JsonResponse["success"] = false;
      JsonResponse["message"] = strcat ("No valid service specified: ", service);
  }
  
  serializeJson(JsonResponse, Serial);
  Serial.println();
}


void Cmd_GetState(CommandParameter &Parameters)
{
  // Allocate the JSON document
  StaticJsonDocument<200> JsonResponse;
  JsonResponse["success"] = true;

  JsonResponse["temperature"] = state.temperature;
  JsonResponse["humidity"] = state.humidity;
  JsonResponse["light"] = state.light;
  JsonResponse["cool"] = state.cool;
  JsonResponse["heat"] = state.heat;
  JsonResponse["humidify"] = state.humidify;
  JsonResponse["dehumidify"] = state.dehumidify;
  JsonResponse["airpump"] = state.airpump;
  JsonResponse["circulate"] = state.circulate;  
  JsonResponse["isactive"] = state.isactive;
  
  JsonArray data = JsonResponse.createNestedArray("loadcells");
  data.add(state.loadcells[0]);
  data.add(state.loadcells[1]);
  data.add(state.loadcells[2]);
  data.add(state.loadcells[3]);
  data.add(state.loadcells[4]);

  serializeJsonPretty(JsonResponse, Serial);
}

void Cmd_GetSettings(CommandParameter &Parameters)
{
  // Allocate the JSON document
  StaticJsonDocument<200> JsonResponse;
  JsonResponse["success"] = true;

  JsonResponse["temperature_target"] = settings.Data.temperature_target;
  JsonResponse["temperature_variance"] = settings.Data.temperature_variance;
  JsonResponse["humidity_target"] = settings.Data.humidity_target;
  JsonResponse["humidity_variance"] = settings.Data.humidity_variance;
  JsonResponse["cycle_delay"] = settings.Data.cycle_delay;

  JsonResponse["load_calibration_1"] = settings.Data.load_calibration_1;
  JsonResponse["load_calibration_2"] = settings.Data.load_calibration_2;
  JsonResponse["load_calibration_3"] = settings.Data.load_calibration_3;
  JsonResponse["load_calibration_4"] = settings.Data.load_calibration_4;
  JsonResponse["load_calibration_5"] = settings.Data.load_calibration_5;
  
  JsonResponse["tare_offset_1"] = settings.Data.tare_offset_1;
  JsonResponse["tare_offset_2"] = settings.Data.tare_offset_2;
  JsonResponse["tare_offset_3"] = settings.Data.tare_offset_3;
  JsonResponse["tare_offset_4"] = settings.Data.tare_offset_4;
  JsonResponse["tare_offset_5"] = settings.Data.tare_offset_5;
  
  serializeJsonPretty(JsonResponse, Serial);
}

void Cmd_TareLoadCell(CommandParameter &Parameters)
{
  int loadcelltotare = atoi(Parameters.NextParameter());
  
  // Allocate the JSON document
  StaticJsonDocument<200> JsonResponse;
  JsonResponse["success"] = true;
  JsonResponse["message"] = "Starting tare 1 loadcell: " + loadcelltotare;

  
  switch(loadcelltotare){
    case 1:
      LoadCell_1.tareNoDelay();
      state.tareloadcell_1 = true;
      break;
    case 2:
      LoadCell_2.tareNoDelay();
      state.tareloadcell_2 = true;
      break;
    case 3:
      LoadCell_3.tareNoDelay();
      state.tareloadcell_3 = true;
      break;
    case 4:
      LoadCell_4.tareNoDelay();
      state.tareloadcell_4 = true;
      break;
    case 5:
      LoadCell_5.tareNoDelay();
      state.tareloadcell_5 = true;
      break;
    default:
      JsonResponse["success"] = false;
      JsonResponse["message"] = "No valid loadcell specified: " + loadcelltotare;
      
  }
  
  serializeJsonPretty(JsonResponse, Serial);
}

//!calibrateloadcell 1 920\r\n (grams)
void Cmd_CalibrateLoadCell(CommandParameter &Parameters)
{
  int loadcelltocalibrate = atoi(Parameters.NextParameter());
  int known_mass = atoi(Parameters.NextParameter());
  
  // Allocate the JSON document
  StaticJsonDocument<200> JsonResponse;
  JsonResponse["success"] = true;
  String message = "Calibrated loadcell: " + loadcelltocalibrate;
  message.concat(" Known mass: ");
  message.concat(known_mass);
  JsonResponse["message"] = message;
  
  if (known_mass > 0 && known_mass < 8000 ){
    switch(loadcelltocalibrate){
      case 1:
        LoadCell_1.refreshDataSet();
        settings.Data.load_calibration_1 = LoadCell_1.getNewCalibration(known_mass);
        settings.Save();
        break;
      case 2:
        LoadCell_2.refreshDataSet();
        settings.Data.load_calibration_2 = LoadCell_2.getNewCalibration(known_mass);
        settings.Save();
        break;
      case 3:
        LoadCell_3.refreshDataSet();
        settings.Data.load_calibration_3 = LoadCell_3.getNewCalibration(known_mass);
        settings.Save();
        break;
      case 4:
        LoadCell_4.refreshDataSet();
        settings.Data.load_calibration_4 = LoadCell_4.getNewCalibration(known_mass);
        settings.Save();
        break;
      case 5:
        LoadCell_5.refreshDataSet();
        settings.Data.load_calibration_5 = LoadCell_5.getNewCalibration(known_mass);
        settings.Save();
        break;
      default:
        JsonResponse["success"] = false;
        JsonResponse["message"] = "No valid loadcell specified: " + loadcelltocalibrate;
        
    }
  }else{
    JsonResponse["message"] = "No valid known mass: " + known_mass;
  }
  
  serializeJsonPretty(JsonResponse, Serial);
}

bool CheckTempAndHumidity(void *) {
#ifdef DEBUG
  Serial.println("Checking Temp & Humidity");
#endif
  
  // Reading temperature or humidity takes about 250 milliseconds!
  // Sensor readings may also be up to 2 seconds 'old' (its a very slow sensor)
  float h = dht.readHumidity();
  // Read temperature as Celsius (the default)
  float t = dht.readTemperature();

  // Check if any reads failed and exit early (to try again).
  if (isnan(h) || isnan(t)) {
#ifdef DEBUG
    Serial.println(F("Failed to read from DHT sensor!"));
#endif
    return true;
  }else{
    state.temperature = t;
    state.humidity = h;
  }
  return true;//Returning true repeats the timer that called this
}

bool CheckLoadCells(void *) {
#ifdef DEBUG
  Serial.println("Checking Load Cells");
#endif

  //get smoothed value from data set
  if (state.newdataloadcell_1) {
      //state.loadcells[0] = LoadCell_1.getData();
      state.loadcells[0] = avgloadcell_1.reading(LoadCell_1.getData()); 
 #ifdef DEBUG
      Serial.print("Load_cell 1 output val: ");
      Serial.println(state.loadcells[0]);
 #endif
      state.newdataloadcell_1 = false;
  }
    if (state.newdataloadcell_2) {
      //state.loadcells[1] = LoadCell_2.getData();
      state.loadcells[1] = avgloadcell_2.reading(LoadCell_2.getData()); 
 #ifdef DEBUG
      Serial.print("Load_cell 2 output val: ");
      Serial.println(state.loadcells[1]);
 #endif
      state.newdataloadcell_2 = false;
  }
    if (state.newdataloadcell_3) {
      //state.loadcells[2] = LoadCell_3.getData();
      state.loadcells[2] = avgloadcell_3.reading(LoadCell_3.getData()); 
 #ifdef DEBUG
      Serial.print("Load_cell 3 output val: ");
      Serial.println(state.loadcells[2]);
 #endif
      state.newdataloadcell_3 = false;
  }
    if (state.newdataloadcell_4) {
      //state.loadcells[3] = LoadCell_4.getData();
      state.loadcells[3] = avgloadcell_4.reading(LoadCell_4.getData()); 
 #ifdef DEBUG
      Serial.print("Load_cell 4 output val: ");
      Serial.println(state.loadcells[3]);
 #endif
      state.newdataloadcell_4 = false;
  }
    if (state.newdataloadcell_5) {
      //state.loadcells[4] = LoadCell_5.getData();
      state.loadcells[4] = avgloadcell_5.reading(LoadCell_5.getData()); 
 #ifdef DEBUG
      Serial.print("Load_cell 5 output val: ");
      Serial.println(state.loadcells[4]);
 #endif
      state.newdataloadcell_5 = false;
  }
  
  return true;//Returning true repeats the timer that called this
}

//Setup & Loop
void setup() {
  Serial.begin(9600);
  while (!Serial) continue;
  Serial.println("Starting...");

  ///START TEMPERATURE & HUMIDITY SENSOR
  dht.begin();
  
  ///START TIMER TO CHECK TEMP & HUMIDITY
  timer.every(10 * 1000, CheckTempAndHumidity);

  ///START TIMER TO CHECK LOADCELLS
  timer.every(15 * 1000, CheckLoadCells);

  //CONFIGURE RELAYS
  pinMode(light_relayenable, OUTPUT);
  digitalWrite( light_relayenable , HIGH);
  pinMode(cool_relayenable, OUTPUT);
  digitalWrite( cool_relayenable , HIGH);
  pinMode(heat_relayenable, OUTPUT);
  digitalWrite( heat_relayenable , HIGH);
  pinMode(humidify_relayenable, OUTPUT);
  digitalWrite( humidify_relayenable , HIGH);
  pinMode(dehumidify_relayenable, OUTPUT);
  digitalWrite( dehumidify_relayenable , HIGH);
  pinMode(airpump_relayenable, OUTPUT);
  digitalWrite( airpump_relayenable , HIGH);
  pinMode(circulate_relayenable, OUTPUT);
  digitalWrite( circulate_relayenable , HIGH);

  ///START SETUP COMMAND HANDLER
  SerialCommandHandler.AddCommand(F("echo"), Cmd_Echo);
  SerialCommandHandler.AddCommand(F("get"), Cmd_Get);
  SerialCommandHandler.AddCommand(F("set"), Cmd_Set);
  //3
  
  SerialCommandHandler.AddCommand(F("settemperaturetarget"), Cmd_SetTemperatureTarget);
  SerialCommandHandler.AddCommand(F("settemperaturevariance"), Cmd_SetTemperatureVariance);
  SerialCommandHandler.AddCommand(F("sethumiditytarget"), Cmd_SetHumidityTarget);
  SerialCommandHandler.AddCommand(F("sethumidityvariance"), Cmd_SetHumidityVariance);
  //7
  
  SerialCommandHandler.AddCommand(F("tareloadcell"), Cmd_TareLoadCell);
  SerialCommandHandler.AddCommand(F("calibrateloadcell"), Cmd_CalibrateLoadCell);
  //9
  
  SerialCommandHandler.AddCommand(F("getstate"), Cmd_GetState);
  SerialCommandHandler.AddCommand(F("getsettings"), Cmd_GetSettings);
  //11
  
  SerialCommandHandler.SetDefaultHandler(Cmd_Unknown);
  //12
  ///END SETUP COMMAND HANDLER

  ///START LOAD CELL SETUP
  LoadCell_1.begin();
  LoadCell_2.begin();
  LoadCell_3.begin();
  LoadCell_4.begin();
  LoadCell_5.begin();
  //start the moving average objects
  avgloadcell_1.begin();
  avgloadcell_2.begin();
  avgloadcell_3.begin();
  avgloadcell_4.begin();
  avgloadcell_5.begin();
  

  boolean _tare = false; //set this to false if you don't want tare to be performed in the next step
  byte loadcell_1_rdy = 0;
  byte loadcell_2_rdy = 0;
  byte loadcell_3_rdy = 0;
  byte loadcell_4_rdy = 0;
  byte loadcell_5_rdy = 0;
  
  //delay(2000);
  while ((loadcell_1_rdy ) < 1) { // + loadcell_2_rdy + loadcell_3_rdy + loadcell_4_rdy + loadcell_5_rdy) < 1) { //run startup, stabilization and tare on all modules simultaniously
    if (!loadcell_1_rdy) loadcell_1_rdy = LoadCell_1.startMultiple(stabilizingtime, _tare);
    if (!loadcell_2_rdy) loadcell_2_rdy = LoadCell_2.startMultiple(stabilizingtime, _tare);
    if (!loadcell_3_rdy) loadcell_3_rdy = LoadCell_3.startMultiple(stabilizingtime, _tare);
    if (!loadcell_4_rdy) loadcell_4_rdy = LoadCell_4.startMultiple(stabilizingtime, _tare);
    if (!loadcell_5_rdy) loadcell_5_rdy = LoadCell_5.startMultiple(stabilizingtime, _tare);
  }
  //delay(10000);
  
  if (LoadCell_1.getTareTimeoutFlag()) {
    Serial.println("Timeout, check MCU>HX711 no.1 wiring and pin designations");
  }
  if (LoadCell_2.getTareTimeoutFlag()) {
    Serial.println("Timeout, check MCU>HX711 no.2 wiring and pin designations");
  }
  if (LoadCell_3.getTareTimeoutFlag()) {
    Serial.println("Timeout, check MCU>HX711 no.3 wiring and pin designations");
  }
  if (LoadCell_4.getTareTimeoutFlag()) {
    Serial.println("Timeout, check MCU>HX711 no.4 wiring and pin designations");
  }
  if (LoadCell_5.getTareTimeoutFlag()) {
    Serial.println("Timeout, check MCU>HX711 no.5 wiring and pin designations");
  }
  Serial.print("settings.Data.load_calibration_1: ");
  Serial.println(settings.Data.load_calibration_1);
  LoadCell_1.setCalFactor(settings.Data.load_calibration_1); // user set calibration value (float)
  LoadCell_2.setCalFactor(settings.Data.load_calibration_2); // user set calibration value (float)
  LoadCell_3.setCalFactor(settings.Data.load_calibration_3); // user set calibration value (float)
  LoadCell_4.setCalFactor(settings.Data.load_calibration_4); // user set calibration value (float)
  LoadCell_5.setCalFactor(settings.Data.load_calibration_5); // user set calibration value (float)

  //need to set the tare offset based on the last tare before weight is applied so that our existing weight does not get Tare'd to 0
  LoadCell_1.setTareOffset( settings.Data.tare_offset_1 );
  LoadCell_2.setTareOffset( settings.Data.tare_offset_2 );
  LoadCell_3.setTareOffset( settings.Data.tare_offset_3 );
  LoadCell_4.setTareOffset( settings.Data.tare_offset_4 );
  LoadCell_5.setTareOffset( settings.Data.tare_offset_5 );
  ///END LOAD CELL SETUP

}

void loop() {
  //tick the timer
  timer.tick();
  
  // Check for serial commands and dispatch them.
  SerialCommandHandler.Process();

  if (state.tareloadcell_1){
    //check if last tare operation is complete
    if (LoadCell_1.getTareStatus() == true) {
      state.tareloadcell_1 = false;
      Serial.println("Tare load cell 1 complete");
      settings.Data.tare_offset_1 = LoadCell_1.getTareOffset();
      settings.Save();
      avgloadcell_1.reset();//reset the moving average object
    }
  }
  if (state.tareloadcell_2){
    //check if last tare operation is complete
    if (LoadCell_2.getTareStatus() == true) {
      state.tareloadcell_2 = false;
      Serial.println("Tare load cell 2 complete");
      settings.Data.tare_offset_2 = LoadCell_2.getTareOffset();
      settings.Save();
      avgloadcell_2.reset();//reset the moving average object
    }
  }
  if (state.tareloadcell_3){
    //check if last tare operation is complete
    if (LoadCell_3.getTareStatus() == true) {
      state.tareloadcell_3 = false;
      Serial.println("Tare load cell 3 complete");
      settings.Data.tare_offset_3 = LoadCell_3.getTareOffset();
      settings.Save();
      avgloadcell_3.reset();//reset the moving average object
    }
  }
  if (state.tareloadcell_4){
    //check if last tare operation is complete
    if (LoadCell_4.getTareStatus() == true) {
      state.tareloadcell_4 = false;
      Serial.println("Tare load cell 4 complete");
      settings.Data.tare_offset_4 = LoadCell_4.getTareOffset();
      settings.Save();
      avgloadcell_4.reset();//reset the moving average object
    }
  }
  if (state.tareloadcell_5){
    //check if last tare operation is complete
    if (LoadCell_5.getTareStatus() == true) {
      state.tareloadcell_5 = false;
      Serial.println("Tare load cell 5 complete");
      settings.Data.tare_offset_5 = LoadCell_5.getTareOffset();
      settings.Save();
      avgloadcell_5.reset();//reset the moving average object
    }
  }

// static boolean newDataReady = 0;
// const int serialPrintInterval = 15000; //increase value to slow down serial print activity
  
//We need to keep calling update to keep data fresh
if (LoadCell_1.update()) state.newdataloadcell_1 = true;
if (LoadCell_2.update()) state.newdataloadcell_2 = true;
if (LoadCell_3.update()) state.newdataloadcell_3 = true;
if (LoadCell_4.update()) state.newdataloadcell_4 = true;
if (LoadCell_5.update()) state.newdataloadcell_5 = true;

}
